# Fritzing sketch fritzing (saved by Fritzing 0.9.3b)

parts:
  MCU1 = Raspberry Pi Zero
  Teensy_3_1 = Teensy 3.1
  C1 = Capacitor Polarized [package=cpol-radial-10uf-25v]
  C3 = Capacitor [package=cap-pth-small-kit]
  C2 = Capacitor [package=cap-pth-small-kit]
  Voltage_Offset = OP37 - Low Noise, Precision, High Speed Op Amp [part_number=OP37]
  R1 = Resistor [tolerance=±5% resistance=8.2k package=THT]
  R2 = Resistor [tolerance=±5% resistance=3.9k package=THT]
  Amplifier = OP37 - Low Noise, Precision, High Speed Op Amp [part_number=OP37]
  R3 = Resistor [tolerance=±5% resistance=1k package=THT]
  C4 = Ceramic Capacitor [capacitance=4.7nF package="100 mil [THT, multilayer]"]
  R4 = Resistor [tolerance=±5% resistance=16k package=THT]
  C5 = Ceramic Capacitor [capacitance=470pF package="100 mil [THT, multilayer]"]
  C6 = Ceramic Capacitor [capacitance=470pF package="100 mil [THT, multilayer]"]
  Comparator = Dual Op-Amp [package=dip08]
  R5 = Resistor [tolerance=±5% resistance=1k package=THT]
  R6 = Resistor [tolerance=±5% resistance=1k package=THT]
  R7 = Resistor [tolerance=±5% resistance=1k package=THT]
  R8 = Resistor [tolerance=±5% resistance=1.6k package=THT]
  R9 = Resistor [tolerance=±5% resistance=16k package=THT]
  C9 = Ceramic Capacitor [capacitance=10nF package="100 mil [THT, multilayer]"]
  C7 = Ceramic Capacitor [capacitance=10nF package="100 mil [THT, multilayer]"]
  IC2 = 4786 4 x 2 Input XOR Gate, multi-part [part_number=4786 package="DIP (Dual Inline) [THT]"]
  Part1 = 4786 4 x 2 Input XOR Gate, multi-part [part_number=4786 package="DIP (Dual Inline) [THT]"]
  IC2_1 = 4786 4 x 2 Input XOR Gate, multi-part [part_number=4786 package="DIP (Dual Inline) [THT]"]
  IC2_2 = 4786 4 x 2 Input XOR Gate, multi-part [part_number=4786 package="DIP (Dual Inline) [THT]"]
  IC2_3 = 4786 4 x 2 Input XOR Gate, multi-part [part_number=4786 package="DIP (Dual Inline) [THT]"]  # not connected
  IC2_4 = 4786 4 x 2 Input XOR Gate, multi-part [part_number=4786 package="DIP (Dual Inline) [THT]"]  # not connected
  R10 = Resistor [tolerance=±5% resistance=16k package=THT]
  R11 = Resistor [tolerance=±5% resistance=1.6k package=THT]
  R12 = Resistor [tolerance=±5% resistance=1k package=THT]
  C10 = Ceramic Capacitor [capacitance=10nF package="100 mil [THT, multilayer]"]
  C11 = Ceramic Capacitor [capacitance=10nF package="100 mil [THT, multilayer]"]
  Transmitter = Piezo Speaker
  Receiver = Piezo Speaker

nets:
  VIN: MCU1.pin_4, Teensy_3_1.Vin, C1.+, C3.1, C2.1, Voltage_Offset.V+, R1.Pin_0, Amplifier.V+, Comparator.A_V+, R5.Pin_0, R6.Pin_0, IC2.connector13, Part1.VDD
  GND: MCU1.pin_6, MCU1.pin_39, Teensy_3_1.GND, C1.-, C3.2, C2.2, Voltage_Offset.-V, R2.Pin_1, Amplifier.-V, Comparator.A_V-, R8.Pin_1, C9.1, C7.0, IC2.connector6, Part1.GND, R11.Pin_1, C10.0, C11.1, Transmitter.pin1, Receiver.pin1
  N1: MCU1.pin_8, Teensy_3_1.D0
  N2: MCU1.pin_10, Teensy_3_1.D1
  N3: Teensy_3_1.D5, IC2.connector3, IC2_2.A2
  N4: Teensy_3_1.D6, IC2.connector0, IC2_1.A1
  N5: Teensy_3_1.A0/D14, R10.Pin_1, C10.1, C11.0
  N6: Teensy_3_1.A1/D15, R9.Pin_1, C9.0, C7.1
  N7: Teensy_3_1.A9/D23, Transmitter.pin2
  N8: Voltage_Offset.-IN, Voltage_Offset.OUT, Amplifier.+IN, Comparator.A_-IN, Comparator.B_-IN
  N9: Voltage_Offset.+IN, R1.Pin_1, R2.Pin_0
  N10: Amplifier.-IN, R3.Pin_1, R4.Pin_0, C5.1
  N11: Amplifier.OUT, R4.Pin_1, C6.0, Comparator.A_+IN, Comparator.B_+IN
  N12: R3.Pin_0, C4.0
  N13: C4.1, Receiver.pin2
  N14: C5.0, C6.1
  N15: Comparator.A_OUT, R5.Pin_1, IC2.connector4, IC2_2.B2
  N16: Comparator.B_OUT, R6.Pin_1, IC2.connector1, IC2_1.B1
  N17: R7.Pin_0, IC2.connector5, IC2_2.Q2
  N18: R7.Pin_1, R8.Pin_0, R9.Pin_0
  N19: IC2.connector2, IC2_1.Q1, R12.Pin_0
  N20: R10.Pin_0, R11.Pin_0, R12.Pin_1

custom parts:
  4786 4 x 2 Input XOR Gate, multi-part: 4786 4 x 2 Input XOR Gate with sub-parts
  4786 4 x 2 Input XOR Gate, multi-part: 4786 4 x 2 Input XOR Gate with sub-parts
  4786 4 x 2 Input XOR Gate, multi-part: 4786 4 x 2 Input XOR Gate with sub-parts
  4786 4 x 2 Input XOR Gate, multi-part: 4786 4 x 2 Input XOR Gate with sub-parts
  4786 4 x 2 Input XOR Gate, multi-part: 4786 4 x 2 Input XOR Gate with sub-parts
  4786 4 x 2 Input XOR Gate, multi-part: 4786 4 x 2 Input XOR Gate with sub-parts
